// Logisim project CIPHA16.circ as structural Verilog: 5 circuits, main circuit main
module main (
  input  in_1
);

  wire clock_1_out, cu_1_pc_sel, cu_1_pc_write, cu_1_ram_sel, cu_1_ram_we, cu_1_regfile_sel, cu_1_regfile_we,
       demultiplexer_1_out1, demultiplexer_1_out2, demultiplexer_1_out3, demultiplexer_1_out4;
  wire [3:0] cu_1_alu_opcode, cu_1_out_device, cu_1_reada, cu_1_readb, cu_1_regfile_waddr, regfile_1_outb,
       regfile_1_outb_2, regfile_1_outb_3;
  wire [7:0] cu_1_alu_imm, cu_1_ram_addr, multiplexer_1_out;
  wire [11:0] alu_1_pc_out, cu_1_pc_out, multiplexer_2_out, pc_1_pc_out;
  wire [15:0] alu_1_aluout, joystick_1_x, multiplexer_3_out, multiplexer_4_out, ram_1_dout, regfile_1_outa,
       register_1_q, register_2_q, rom_1_data;
  wire [15:12] regfile_1_outb_4;

  Clock clock_1 (.out(clock_1_out));
  ROM #(.addrWidth(12), .dataWidth(16)) rom_1 (.addr(pc_1_pc_out), .data(rom_1_data));
  Multiplexer #(.width(8)) multiplexer_1 (
    .in0(cu_1_ram_addr), .in1(regfile_1_outa[7:0]), .out(multiplexer_1_out), .sel(cu_1_ram_sel));
  CU cu_1 (
    .clk(clock_1_out), .Instruction_in(rom_1_data), .RAM_WE(cu_1_ram_we), .RAM_Addr(cu_1_ram_addr),
    .PC_Write(cu_1_pc_write), .PC_Out(cu_1_pc_out), .ReadA(cu_1_reada), .ReadB(cu_1_readb),
    .RegFile_WE(cu_1_regfile_we), .RegFile_WAddr(cu_1_regfile_waddr), .RegFile_Sel(cu_1_regfile_sel),
    .RAM_Sel(cu_1_ram_sel), .PC_Sel(cu_1_pc_sel), .ALU_Opcode(cu_1_alu_opcode), .ALU_Imm(cu_1_alu_imm),
    .Out_Device(cu_1_out_device), .Display_Reset(in_1));
  Multiplexer #(.width(12)) multiplexer_2 (
    .in0(alu_1_pc_out), .in1(cu_1_pc_out), .out(multiplexer_2_out), .sel(cu_1_pc_sel));
  Multiplexer #(.width(16)) multiplexer_3 (
    .in0(alu_1_aluout), .in1(ram_1_dout), .out(multiplexer_3_out), .sel(cu_1_regfile_sel));
  PC pc_1 (.load(cu_1_pc_write), .clk(clock_1_out), .reset(in_1), .pc_in(multiplexer_2_out), .pc_out(pc_1_pc_out));
  RegFile regfile_1 (
    .ReadB(cu_1_readb), .ReadA(cu_1_reada), .clk(clock_1_out), .WData(multiplexer_3_out),
    .WAddr(cu_1_regfile_waddr), .WE(cu_1_regfile_we), .Extern_Inp(joystick_1_x), .OutA(regfile_1_outa),
    .OutB({regfile_1_outb_4, regfile_1_outb_3, regfile_1_outb_2, regfile_1_outb}));
  Demultiplexer #(.select(4)) demultiplexer_1 (
    .out1(demultiplexer_1_out1), .out2(demultiplexer_1_out2), .out3(demultiplexer_1_out3),
    .out4(demultiplexer_1_out4), .in(1'b1), .sel(cu_1_out_device));  // open: out0, out5, out6, out7, out8, out9, out10, out11, out12, out13, out14, out15
  RAM #(.asyncread("true"), .dataWidth(16)) ram_1 (
    .addr(multiplexer_1_out), .we(cu_1_ram_we), .oe(clock_1_out), .clk(clock_1_out),
    .din({regfile_1_outb_4, regfile_1_outb_3, regfile_1_outb_2, regfile_1_outb}), .dout(ram_1_dout));
  ALU alu_1 (
    .Opcode(cu_1_alu_opcode), .InA(regfile_1_outa),
    .InB({regfile_1_outb_4, regfile_1_outb_3, regfile_1_outb_2, regfile_1_outb}), .Imm(cu_1_alu_imm),
    .PC_In(pc_1_pc_out), .ALUOut(alu_1_aluout), .PC_Out(alu_1_pc_out));
  // RGB_Video #(.height(16), .scale(8), .width(16)) rgb_video_1: pin names not known; wires that end beside it: in_1, clock_1_out, demultiplexer_1_out1, regfile_1_outb, regfile_1_outb_2, regfile_1_outb_3
  Register #(.width(16)) register_1 (
    .D({regfile_1_outb_4, regfile_1_outb_3, regfile_1_outb_2, regfile_1_outb}), .en(demultiplexer_1_out3),
    .clk(clock_1_out), .Q(register_1_q));  // open: clr
  Multiplexer #(.width(16)) multiplexer_4 (
    .in0({16{1'b0}}), .in1({regfile_1_outb_4, regfile_1_outb_3, regfile_1_outb_2, regfile_1_outb}),
    .out(multiplexer_4_out), .sel(demultiplexer_1_out4));
  Register #(.width(16)) register_2 (
    .D(multiplexer_4_out), .en(demultiplexer_1_out4), .clk(clock_1_out), .Q(register_2_q), .clr(in_1));
  Joystick #(.bits(2)) joystick_1 (.x(joystick_1_x[1:0]), .y(joystick_1_x[7:6]));
  TTY tty_1 (
    .data({regfile_1_outb_2[2:0], regfile_1_outb}), .clk(clock_1_out), .we(demultiplexer_1_out2),
    .clr(regfile_1_outb_2[3]));
  Hex_Digit_Display hex_digit_display_1 (.value(register_2_q[15:12]));  // open: dp
  // RGBLED rgbled_1: pin names not known; wires that end beside it: register_1_q[1], register_1_q[0], register_1_q[2]
  Hex_Digit_Display hex_digit_display_2 (.value(register_2_q[11:8]));  // open: dp
  Hex_Digit_Display hex_digit_display_3 (.value(register_2_q[7:4]));  // open: dp
  Hex_Digit_Display hex_digit_display_4 (.value(register_2_q[3:0]));  // open: dp

  // Notes on the sheet:
  //   contents of rom_1 (hex, n*v repeats v):
  //   a101 d301 e000 121 e002
endmodule

module PC (
  input  clk,
  input  reset,
  input  [11:0] pc_in,
  input  load,
  output [11:0] pc_out
);

  wire [11:0] adder_1_out, multiplexer_1_out, multiplexer_2_out;

  Multiplexer #(.width(12)) multiplexer_1 (.in0(adder_1_out), .in1({12{1'b0}}), .out(multiplexer_1_out), .sel(reset));
  Multiplexer #(.width(12)) multiplexer_2 (.in0(multiplexer_1_out), .in1(pc_in), .out(multiplexer_2_out), .sel(load));
  Adder #(.width(12)) adder_1 (.a(pc_out), .b(12'h1), .out(adder_1_out));  // open: cin, cout
  Register #(.width(12)) register_1 (.D(multiplexer_2_out), .en(clk), .clk(clk), .Q(pc_out));  // open: clr
endmodule

module CU (
  input  clk,
  input  [15:0] Instruction_in,
  output RAM_WE,
  output [7:0] RAM_Addr,
  output PC_Write,
  output [11:0] PC_Out,
  output [3:0] ReadA,
  output [3:0] ReadB,
  output RegFile_WE,
  output [3:0] RegFile_WAddr,
  output RegFile_Sel,
  output RAM_Sel,
  output PC_Sel,
  output [3:0] ALU_Opcode,
  output [7:0] ALU_Imm,
  output [3:0] Out_Device,
  output Display_Reset
);

  wire and_1_out, and_2_out, and_3_out, comparator_1_eq, comparator_2_eq, comparator_3_gt, comparator_4_lt,
       comparator_5_eq, comparator_6_lt, comparator_7_eq, comparator_8_eq, comparator_9_eq, comparator_10_eq,
       comparator_11_eq, comparator_12_eq;

  Comparator #(.mode("unsigned"), .width(4)) comparator_1 (
    .a(Instruction_in[15:12]), .b(4'b1100), .eq(comparator_1_eq));  // open: gt, lt
  Comparator #(.mode("unsigned"), .width(4)) comparator_2 (
    .a(Instruction_in[15:12]), .b(4'b1111), .eq(comparator_2_eq));  // open: gt, lt
  Comparator #(.mode("unsigned"), .width(4)) comparator_3 (
    .a(Instruction_in[15:12]), .b(4'b0101), .gt(comparator_3_gt));  // open: eq, lt
  Comparator #(.mode("unsigned"), .width(4)) comparator_4 (
    .a(Instruction_in[15:12]), .b(4'b1010), .lt(comparator_4_lt));  // open: gt, eq
  Comparator #(.mode("unsigned"), .width(4)) comparator_5 (
    .a(Instruction_in[15:12]), .b(4'b1110), .eq(comparator_5_eq));  // open: gt, lt
  Comparator #(.mode("unsigned"), .width(4)) comparator_6 (
    .a(Instruction_in[15:12]), .b(4'b0110), .lt(comparator_6_lt));  // open: gt, eq
  Comparator #(.mode("unsigned"), .width(4)) comparator_7 (
    .a(Instruction_in[15:12]), .b(4'b1010), .eq(comparator_7_eq));  // open: gt, lt
  Comparator #(.mode("unsigned"), .width(4)) comparator_8 (
    .a(Instruction_in[15:12]), .b(4'b1111), .eq(comparator_8_eq));  // open: gt, lt
  Comparator #(.mode("unsigned"), .width(4)) comparator_9 (
    .a(Instruction_in[15:12]), .b(4'b1011), .eq(comparator_9_eq));  // open: gt, lt
  and and_1 (and_1_out, comparator_2_eq, Instruction_in[8]);
  and and_2 (and_2_out, comparator_3_gt, comparator_4_lt);
  and and_3 (and_3_out, comparator_8_eq, Instruction_in[8]);
  Comparator #(.mode("unsigned"), .width(4)) comparator_10 (
    .a(Instruction_in[15:12]), .b(4'b1101), .eq(comparator_10_eq));  // open: gt, lt
  or or_1 (RAM_WE, comparator_1_eq, and_1_out);
  or or_2 (PC_Write, and_2_out, comparator_5_eq);
  Multiplexer #(.width(4)) multiplexer_1 (
    .in0(4'b0000), .in1(Instruction_in[11:8]), .out(Out_Device), .sel(comparator_10_eq));
  or or_3 (RegFile_WE, comparator_6_lt, and_3_out, comparator_7_eq, comparator_9_eq);
  Comparator #(.mode("unsigned"), .width(4)) comparator_11 (
    .a(Instruction_in[15:12]), .b(4'b1111), .eq(comparator_11_eq));  // open: gt, lt
  Comparator #(.mode("unsigned"), .width(4)) comparator_12 (
    .a(Instruction_in[15:12]), .b(4'b1011), .eq(comparator_12_eq));  // open: gt, lt
  Comparator #(.mode("unsigned"), .width(4)) comparator_13 (
    .a(Instruction_in[15:12]), .b(4'b1101), .gt(PC_Sel));  // open: eq, lt
  or or_4 (RegFile_Sel, comparator_11_eq, comparator_12_eq);
  Comparator #(.mode("unsigned"), .width(4)) comparator_14 (
    .a(Instruction_in[15:12]), .b(4'b1111), .eq(RAM_Sel));  // open: gt, lt

  assign ALU_Imm = Instruction_in[7:0];
  assign ALU_Opcode = Instruction_in[15:12];
  assign PC_Out = Instruction_in[11:0];
  assign RAM_Addr = Instruction_in[11:4];
  assign ReadA = Instruction_in[7:4];
  assign ReadB = Instruction_in[3:0];
  assign RegFile_WAddr = Instruction_in[11:8];
endmodule

module RegFile (
  input  [3:0] ReadB,
  input  [3:0] ReadA,
  input  clk,
  input  [15:0] WData,
  input  [3:0] WAddr,
  input  WE,
  input  [15:0] Extern_Inp,
  output [15:0] OutA,
  output [15:0] OutB
);

  wire demultiplexer_1_out0, demultiplexer_1_out1, demultiplexer_1_out2, demultiplexer_1_out3,
       demultiplexer_1_out4, demultiplexer_1_out5, demultiplexer_1_out6, demultiplexer_1_out7,
       demultiplexer_1_out8, demultiplexer_1_out9, demultiplexer_1_out10, demultiplexer_1_out11,
       demultiplexer_1_out12, demultiplexer_1_out13, demultiplexer_1_out14, demultiplexer_1_out15;
  wire [15:0] demultiplexer_2_out0, demultiplexer_2_out1, demultiplexer_2_out2, demultiplexer_2_out3,
       demultiplexer_2_out4, demultiplexer_2_out5, demultiplexer_2_out6, demultiplexer_2_out7,
       demultiplexer_2_out8, demultiplexer_2_out9, demultiplexer_2_out10, demultiplexer_2_out11,
       demultiplexer_2_out12, demultiplexer_2_out13, demultiplexer_2_out14, register_1_q, register_2_q,
       register_3_q, register_4_q, register_5_q, register_6_q, register_7_q, register_8_q, register_9_q,
       register_10_q, register_11_q, register_12_q, register_13_q, register_14_q, register_15_q;

  Demultiplexer #(.select(4)) demultiplexer_1 (
    .out0(demultiplexer_1_out0), .out1(demultiplexer_1_out1), .out2(demultiplexer_1_out2),
    .out3(demultiplexer_1_out3), .out4(demultiplexer_1_out4), .out5(demultiplexer_1_out5),
    .out6(demultiplexer_1_out6), .out7(demultiplexer_1_out7), .out8(demultiplexer_1_out8),
    .out9(demultiplexer_1_out9), .out10(demultiplexer_1_out10), .out11(demultiplexer_1_out11),
    .out12(demultiplexer_1_out12), .out13(demultiplexer_1_out13), .out14(demultiplexer_1_out14),
    .out15(demultiplexer_1_out15), .in(WE), .sel(WAddr));
  Demultiplexer #(.select(4), .width(16)) demultiplexer_2 (
    .out0(demultiplexer_2_out0), .out1(demultiplexer_2_out1), .out2(demultiplexer_2_out2),
    .out3(demultiplexer_2_out3), .out4(demultiplexer_2_out4), .out5(demultiplexer_2_out5),
    .out6(demultiplexer_2_out6), .out7(demultiplexer_2_out7), .out8(demultiplexer_2_out8),
    .out9(demultiplexer_2_out9), .out10(demultiplexer_2_out10), .out11(demultiplexer_2_out11),
    .out12(demultiplexer_2_out12), .out13(demultiplexer_2_out13), .out14(demultiplexer_2_out14), .in(WData),
    .sel(WAddr));  // open: out15
  Register #(.width(16)) register_1 (
    .D(demultiplexer_2_out0), .en(demultiplexer_1_out0), .clk(clk), .Q(register_1_q));  // open: clr
  Register #(.width(16)) register_2 (
    .D(demultiplexer_2_out1), .en(demultiplexer_1_out1), .clk(clk), .Q(register_2_q));  // open: clr
  Register #(.width(16)) register_3 (
    .D(demultiplexer_2_out2), .en(demultiplexer_1_out2), .clk(clk), .Q(register_3_q));  // open: clr
  Register #(.width(16)) register_4 (
    .D(demultiplexer_2_out3), .en(demultiplexer_1_out3), .clk(clk), .Q(register_4_q));  // open: clr
  Register #(.width(16)) register_5 (
    .D(demultiplexer_2_out4), .en(demultiplexer_1_out4), .clk(clk), .Q(register_5_q));  // open: clr
  Register #(.width(16)) register_6 (
    .D(demultiplexer_2_out5), .en(demultiplexer_1_out5), .clk(clk), .Q(register_6_q));  // open: clr
  Register #(.width(16)) register_7 (
    .D(demultiplexer_2_out6), .en(demultiplexer_1_out6), .clk(clk), .Q(register_7_q));  // open: clr
  Register #(.width(16)) register_8 (
    .D(demultiplexer_2_out7), .en(demultiplexer_1_out7), .clk(clk), .Q(register_8_q));  // open: clr
  Register #(.width(16)) register_9 (
    .D(demultiplexer_2_out8), .en(demultiplexer_1_out8), .clk(clk), .Q(register_9_q));  // open: clr
  Register #(.width(16)) register_10 (
    .D(demultiplexer_2_out9), .en(demultiplexer_1_out9), .clk(clk), .Q(register_10_q));  // open: clr
  Register #(.width(16)) register_11 (
    .D(demultiplexer_2_out10), .en(demultiplexer_1_out10), .clk(clk), .Q(register_11_q));  // open: clr
  Register #(.width(16)) register_12 (
    .D(demultiplexer_2_out11), .en(demultiplexer_1_out11), .clk(clk), .Q(register_12_q));  // open: clr
  Register #(.width(16)) register_13 (
    .D(demultiplexer_2_out12), .en(demultiplexer_1_out12), .clk(clk), .Q(register_13_q));  // open: clr
  Register #(.width(16)) register_14 (
    .D(demultiplexer_2_out13), .en(demultiplexer_1_out13), .clk(clk), .Q(register_14_q));  // open: clr
  Register #(.width(16)) register_15 (
    .D(demultiplexer_2_out14), .en(demultiplexer_1_out14), .clk(clk), .Q(register_15_q));  // open: clr
  Multiplexer #(.select(4), .width(16)) multiplexer_1 (
    .in0(register_1_q), .in1(register_2_q), .in2(register_3_q), .in3(register_4_q), .in4(register_5_q),
    .in5(register_6_q), .in6(register_7_q), .in7(register_8_q), .in8(register_9_q), .in9(register_10_q),
    .in10(register_11_q), .in11(register_12_q), .in12(register_13_q), .in13(register_14_q),
    .in14(register_15_q), .in15(Extern_Inp), .out(OutA), .sel(ReadA));
  Multiplexer #(.select(4), .width(16)) multiplexer_2 (
    .in0(register_1_q), .in1(register_2_q), .in2(register_3_q), .in3(register_4_q), .in4(register_5_q),
    .in5(register_6_q), .in6(register_7_q), .in7(register_8_q), .in8(register_9_q), .in9(register_10_q),
    .in10(register_11_q), .in11(register_12_q), .in12(register_13_q), .in13(register_14_q),
    .in14(register_15_q), .in15(Extern_Inp), .out(OutB), .sel(ReadB));
endmodule

module ALU (
  input  [3:0] Opcode,
  input  [15:0] InA,
  input  [15:0] InB,
  input  [7:0] Imm,
  input  [11:0] PC_In,
  output [15:0] ALUOut,
  output [11:0] PC_Out
);

  wire comparator_1_gt, comparator_2_eq, comparator_2_lt, not_1_out;
  wire [0:0] comparator_1_eq, comparator_1_lt, or_1_out;
  wire [1:0] multiplexer_1_out_2, multiplexer_2_out;
  wire [11:0] adder_3_out, adder_4_out, multiplexer_9_out, multiplexer_10_out, multiplexer_11_out;
  wire [13:0] multiplexer_1_out, multiplexer_2_out_2;
  wire [15:0] adder_1_out, adder_2_out, and_1_out, multiplexer_3_out, multiplexer_4_out, multiplexer_5_out,
       multiplexer_6_out, multiplexer_7_out, multiplexer_8_out, or_2_out, subtractor_1_out;

  Comparator #(.width(16)) comparator_1 (
    .a(InA), .b(InB), .gt(comparator_1_gt), .eq(comparator_1_eq[0]), .lt(comparator_1_lt[0]));
  Comparator #(.width(16)) comparator_2 (.a(InA), .b(InB), .eq(comparator_2_eq), .lt(comparator_2_lt));  // open: gt
  Adder #(.width(16)) adder_1 (.a(InA), .b(InB), .out(adder_1_out));  // open: cin, cout
  Subtractor #(.width(16)) subtractor_1 (.a(InA), .b(InB), .out(subtractor_1_out));  // open: bin, bout
  or or_1 (or_1_out[0], comparator_1_gt, comparator_1_lt[0]);
  Adder #(.width(16)) adder_2 (.a(InB), .b({{8{1'b0}}, Imm}), .out(adder_2_out));  // open: cin, cout
  Adder #(.width(12)) adder_3 (.a({4'b0000, Imm}), .b(PC_In), .out(adder_3_out));  // open: cin, cout
  Multiplexer #(.width(16)) multiplexer_1 (
    .in0(InA), .in1({InA[0], InA[15:1]}), .out({multiplexer_1_out, multiplexer_1_out_2}), .sel(InB[0]));
  Multiplexer #(.width(16)) multiplexer_2 (
    .in0(InA), .in1({InA[14:0], InA[15]}), .out({multiplexer_2_out, multiplexer_2_out_2}), .sel(InB[0]));
  and and_1 (and_1_out[0], InB[0], InA[0]);
  and and_2 (and_1_out[1], InB[1], InA[1]);
  and and_3 (and_1_out[2], InB[2], InA[2]);
  and and_4 (and_1_out[3], InB[3], InA[3]);
  and and_5 (and_1_out[4], InB[4], InA[4]);
  and and_6 (and_1_out[5], InB[5], InA[5]);
  and and_7 (and_1_out[6], InB[6], InA[6]);
  and and_8 (and_1_out[7], InB[7], InA[7]);
  and and_9 (and_1_out[8], InB[8], InA[8]);
  and and_10 (and_1_out[9], InB[9], InA[9]);
  and and_11 (and_1_out[10], InB[10], InA[10]);
  and and_12 (and_1_out[11], InB[11], InA[11]);
  and and_13 (and_1_out[12], InB[12], InA[12]);
  and and_14 (and_1_out[13], InB[13], InA[13]);
  and and_15 (and_1_out[14], InB[14], InA[14]);
  and and_16 (and_1_out[15], InB[15], InA[15]);
  Multiplexer #(.width(16)) multiplexer_3 (
    .in0({multiplexer_1_out, multiplexer_1_out_2}), .in1({multiplexer_1_out_2, multiplexer_1_out}),
    .out(multiplexer_3_out), .sel(InB[1]));
  Multiplexer #(.width(16)) multiplexer_4 (
    .in0({multiplexer_2_out, multiplexer_2_out_2}), .in1({multiplexer_2_out_2, multiplexer_2_out}),
    .out(multiplexer_4_out), .sel(InB[1]));
  Multiplexer #(.width(16)) multiplexer_5 (
    .in0(multiplexer_3_out), .in1({multiplexer_3_out[3:0], multiplexer_3_out[15:4]}),
    .out(multiplexer_5_out), .sel(InB[2]));
  Multiplexer #(.width(16)) multiplexer_6 (
    .in0(multiplexer_4_out), .in1({multiplexer_4_out[11:0], multiplexer_4_out[15:12]}),
    .out(multiplexer_6_out), .sel(InB[2]));
  Multiplexer #(.width(16)) multiplexer_7 (
    .in0(multiplexer_5_out), .in1({multiplexer_5_out[7:0], multiplexer_5_out[15:8]}),
    .out(multiplexer_7_out), .sel(InB[3]));
  Multiplexer #(.width(16)) multiplexer_8 (
    .in0(multiplexer_6_out), .in1({multiplexer_6_out[7:0], multiplexer_6_out[15:8]}),
    .out(multiplexer_8_out), .sel(InB[3]));
  or or_2 (or_2_out[0], InB[0], InA[0]);
  or or_3 (or_2_out[1], InB[1], InA[1]);
  or or_4 (or_2_out[2], InB[2], InA[2]);
  or or_5 (or_2_out[3], InB[3], InA[3]);
  or or_6 (or_2_out[4], InB[4], InA[4]);
  or or_7 (or_2_out[5], InB[5], InA[5]);
  or or_8 (or_2_out[6], InB[6], InA[6]);
  or or_9 (or_2_out[7], InB[7], InA[7]);
  or or_10 (or_2_out[8], InB[8], InA[8]);
  or or_11 (or_2_out[9], InB[9], InA[9]);
  or or_12 (or_2_out[10], InB[10], InA[10]);
  or or_13 (or_2_out[11], InB[11], InA[11]);
  or or_14 (or_2_out[12], InB[12], InA[12]);
  or or_15 (or_2_out[13], InB[13], InA[13]);
  or or_16 (or_2_out[14], InB[14], InA[14]);
  or or_17 (or_2_out[15], InB[15], InA[15]);
  not not_1 (not_1_out, comparator_2_eq);
  Adder #(.width(12)) adder_4 (.a(PC_In), .b(12'h1), .out(adder_4_out));  // open: cin, cout
  Multiplexer #(.width(12)) multiplexer_9 (
    .in0(adder_4_out), .in1(adder_3_out), .out(multiplexer_9_out), .sel(comparator_2_eq));
  Multiplexer #(.width(12)) multiplexer_10 (
    .in0(adder_4_out), .in1(adder_3_out), .out(multiplexer_10_out), .sel(not_1_out));
  Multiplexer #(.width(12)) multiplexer_11 (
    .in0(adder_4_out), .in1(adder_3_out), .out(multiplexer_11_out), .sel(comparator_2_lt));
  Multiplexer #(.select(4), .width(16)) multiplexer_12 (
    .in0(adder_1_out), .in1(subtractor_1_out), .in2(and_1_out), .in3(or_2_out), .in4(multiplexer_8_out),
    .in5(multiplexer_7_out), .in7({{15{1'b0}}, comparator_1_eq[0]}), .in8({{15{1'b0}}, or_1_out[0]}),
    .in9({{15{1'b0}}, comparator_1_lt[0]}), .in10(adder_2_out), .out(ALUOut), .sel(Opcode));  // open: in6, in11, in12, in13, in14, in15
  Multiplexer #(.select(4), .width(12)) multiplexer_13 (
    .in6(InA[11:0]), .in7(multiplexer_9_out), .in8(multiplexer_10_out), .in9(multiplexer_11_out),
    .out(PC_Out), .sel(Opcode));  // open: in0, in1, in2, in3, in4, in5, in10, in11, in12, in13, in14, in15
endmodule
